# Fritzing sketch HardwareSchematicDesign (saved by Fritzing 0.9.3b)
breadboards: 1

parts:
  IC3 = IC, DIP package, 6 pins [chip_label=Mini-USb]
  IC6 = IC, DIP package, 16 pins [chip_label="74VHC153 Multiplexer Bit 2 & 3"]
  IC7 = IC, DIP package, 16 pins [chip_label="74VHC153 Multiplexer Bit 0 & 1"]
  IC8 = IC, DIP package, 16 pins [chip_label="MC14008B-D Adder"]
  IC9 = IC, DIP package, 16 pins [chip_label="MC14076B-D Accumulator"]
  IC10 = IC, DIP package, 14 pins [chip_label="MM74C95 LSL "]
  IC11 = IC, DIP package, 16 pins [chip_label=HEF4543BF-BCD-to-7SegmentDriver]
  7_Segment1 = 7 Segment Display
  IC12 = IC, DIP package, 16 pins [chip_label="MC14076B-D Code Register"]
  IC13 = IC, DIP package, 14 pins [chip_label="74LS266 XNOR"]
  IC14 = IC, DIP package, 14 pins [chip_label="SN74LS08 AND"]
  IC15 = IC, DIP package, 14 pins [chip_label="74LS04 NOT"]
  IC16 = IC, DIP package, 16 pins [chip_label="74VHC153 Multiplexer Bit 0 & 1"]
  IC17 = IC, DIP package, 16 pins [chip_label="MC14076B-D Addr Register"]
  IC18 = IC, DIP package, 14 pins [chip_label="ZC4013B D_FF"]
  LED1 = LED - 5mm [color="Red (633nm)" package="5 mm [THT]"]
  LED2 = LED - 5mm [color="Red (633nm)" package="5 mm [THT]"]
  SW1 = DIP Switch 8 Position [package=dipswitch-08]
  IC19 = IC, DIP package, 16 pins [chip_label="74VHC153 Multiplexer Bit 0 & 1"]
  IC20 = IC, DIP package, 16 pins [chip_label="74VHC153 Multiplexer Bit 2 & 3"]
  IC21 = IC, DIP package, 16 pins [chip_label="74VHC153 Multiplexer Bit 4 & 5"]
  SW2 = DIP Switch 8 Position [package=dipswitch-08]
  SW3 = DIP Switch 8 Position [package=dipswitch-08]
  SW4 = DIP Switch 8 Position [package=dipswitch-08]
  IC22 = IC, DIP package, 14 pins [chip_label="MM74C14 Schmitt Trigger"]
  S1 = Pushbutton [package=THT]
  R1 = Resistor [tolerance=±5% resistance=10k package=THT]
  C1 = Tantalum Capacitor [capacitance=0.1µF package="100 mil [THT, tantalum]"]

nets:
  N1: IC3.pin1, IC6.pin16, IC7.pin16, IC8.pin16, IC10.pin4, IC10.pin6, IC11.pin16, IC12.pin16, IC13.pin2, IC13.pin5, IC13.pin14, IC14.pin14, IC15.pin14, IC16.pin16, IC17.pin16, IC18.pin14, SW1.1, SW1.2, SW1.3, SW1.4, SW1.5, SW1.6, IC19.pin16, IC20.pin16, IC21.pin16, SW2.1, SW2.2, SW2.3, SW2.4, SW2.5, SW2.6, SW3.1, SW3.2, SW3.3, SW3.4, SW3.5, SW3.6, SW4.1, SW4.2, SW4.3, SW4.4, SW4.5, SW4.6, IC22.pin14, R1.Pin_0
  N2: IC3.pin5, IC6.pin8, IC7.pin8, IC8.pin8, IC9.pin8, IC10.pin11, IC11.pin8, IC12.pin8, IC13.pin7, IC14.pin7, IC15.pin7, IC16.pin2, IC16.pin8, IC17.pin8, IC18.pin7, LED1.cathode, LED2.cathode, IC19.pin8, IC20.pin8, IC21.pin8, IC22.pin7
  N3: IC6.pin2, IC7.pin2, IC12.pin4, IC13.pin6
  N4: IC6.pin3, IC8.pin2, IC9.pin5, IC10.pin3, IC11.pin2
  N5: IC6.pin4, IC10.pin10
  N6: IC6.pin5, IC8.pin12
  N7: IC6.pin6, IC8.pin3, IC17.pin5
  N8: IC6.pin7, IC9.pin12
  N9: IC6.pin9, IC9.pin11
  N10: IC6.pin10, IC8.pin1, IC17.pin6
  N11: IC6.pin11, IC8.pin13
  N12: IC6.pin12, IC10.pin9
  N13: IC6.pin13, IC8.pin15, IC9.pin6, IC10.pin5, IC11.pin4
  N14: IC6.pin14, IC7.pin14, IC12.pin3, IC13.pin1
  N15: IC7.pin3, IC8.pin6, IC9.pin3, IC10.pin14, IC11.pin5
  N16: IC7.pin4, IC10.pin13
  N17: IC7.pin5, IC8.pin10
  N18: IC7.pin6, IC8.pin7, IC16.pin5, IC17.pin3
  N19: IC7.pin7, IC9.pin14
  N20: IC7.pin9, IC9.pin13
  N21: IC7.pin10, IC8.pin5, IC16.pin11, IC17.pin4
  N22: IC7.pin11, IC8.pin11
  N23: IC7.pin12, IC10.pin12
  N24: IC7.pin13, IC8.pin4, IC9.pin4, IC10.pin2, IC11.pin3
  N25: IC9.pin7, IC15.pin12, IC18.pin3, IC18.pin11
  N26: IC11.pin9, 7_Segment1.Segment_A
  N27: IC11.pin10, 7_Segment1.Segment_B
  N28: IC11.pin11, 7_Segment1.Segment_C
  N29: IC11.pin12, 7_Segment1.Segment_D
  N30: IC11.pin13, 7_Segment1.Segment_E
  N31: IC11.pin14, 7_Segment1.Segment_F
  N32: IC11.pin15, 7_Segment1.Segment_G
  N33: IC12.pin7, IC15.pin13, IC17.pin7, IC22.pin2
  N34: IC12.pin13, IC21.pin9
  N35: IC12.pin14, IC21.pin7
  N36: IC13.pin3, IC14.pin1
  N37: IC13.pin4, IC14.pin2
  N38: IC13.pin11, IC16.pin6
  N39: IC13.pin12, IC15.pin1, IC18.pin1, LED1.anode, IC19.pin14, IC20.pin14, IC21.pin14
  N40: IC13.pin13, IC18.pin13, LED2.anode, IC19.pin2, IC20.pin2, IC21.pin2
  N41: IC14.pin3, IC16.pin14
  N42: IC15.pin2, IC16.pin10
  N43: IC16.pin7, IC18.pin5
  N44: IC16.pin9, IC18.pin9
  N45: IC17.pin11, IC20.pin9
  N46: IC17.pin12, IC20.pin7
  N47: IC17.pin13, IC19.pin9
  N48: IC17.pin14, IC19.pin7
  N49: SW1.11, IC21.pin10
  N50: SW1.12, IC21.pin6
  N51: SW1.13, IC20.pin10
  N52: SW1.14, IC20.pin6
  N53: SW1.15, IC19.pin10
  N54: SW1.16, IC19.pin6
  N55: IC19.pin3, SW4.16
  N56: IC19.pin4, SW3.16
  N57: IC19.pin5, SW2.16
  N58: IC19.pin11, SW2.15
  N59: IC19.pin12, SW3.15
  N60: IC19.pin13, SW4.15
  N61: IC20.pin3, SW4.14
  N62: IC20.pin4, SW3.14
  N63: IC20.pin5, SW2.14
  N64: IC20.pin11, SW2.13
  N65: IC20.pin12, SW3.13
  N66: IC20.pin13, SW4.13
  N67: IC21.pin3, SW4.12
  N68: IC21.pin4, SW3.12
  N69: IC21.pin5, SW2.12
  N70: IC21.pin11, SW2.11
  N71: IC21.pin12, SW3.11
  N72: IC21.pin13, SW4.11
  N73: IC22.pin1, S1.leg1, R1.Pin_1, C1.+
  N74: S1.leg0, C1.-

notes:
  Multiplexer
  Vdd from Mini-USB
  Pushbutton (CLK)
  Accumulator
  Adder
  Code Register
  =3
  Addr Register
  PC Flip Flop
  NOT
  LEDs
  BCD to 7-seg Driver
  7-seg Display
  Switch 0
  Switch 3
  Switch 2
  Switch 1
  Input D5-0
  D4-5
  D3-0
  D0-1
  LSL
  Multiplexers
